# Fritzing sketch frame (saved by Fritzing 1.0.4)
circuit board: 4cm x 11cm
breadboards: 3

parts:
  100K = Resistor [tolerance=±5% resistance=100k power=0.25W package=THT]  # not connected
  ][1 = PJ-301M [part_number=PJ-301M]
  103 = Ceramic Capacitor [capacitance=10nF voltage=16V package="200 mil [THT, multilayer]"]
  104 = Ceramic Capacitor [capacitance=100nF voltage=16V package="200 mil [THT, multilayer]"]
  J3 = shrouded pin header, 16 pins [form="♂ (shrouded male)"]
  4001 = Diode [package=diode-1n4148]
  Out1 = PJ-301M [part_number=PJ-301M]
  OUT2 = PJ-301M [part_number=PJ-301M]
  ][2 = PJ-301M [part_number=PJ-301M]
  Out3 = PJ-301M [part_number=PJ-301M]
  IN3 = PJ-301M [part_number=PJ-301M]
  IN4 = PJ-301M [part_number=PJ-301M]
  TL074 = TL074 Quad Opamp (Movable) [package="DIP (Dual Inline)"]
  TL074_PWR = TL074 Quad Opamp (Movable) [package="DIP (Dual Inline)"]  # not connected
  TL074_A = TL074 Quad Opamp (Movable) [package="DIP (Dual Inline)"]  # not connected
  TL074_B = TL074 Quad Opamp (Movable) [package="DIP (Dual Inline)"]  # not connected
  TL074_C = TL074 Quad Opamp (Movable) [package="DIP (Dual Inline)"]  # not connected
  TL074_D = TL074 Quad Opamp (Movable) [package="DIP (Dual Inline)"]  # not connected
  Rel = Rotary Potentiometer (Small) [maximum_resistance=100kΩ knob_status=50% power=0.5W package=THT]  # not connected
  Att = Rotary Potentiometer (Small) [maximum_resistance=100kΩ knob_status=50% power=0.5W package=THT]  # not connected
  OUT4 = PJ-301M [part_number=PJ-301M]
  100uF = Electrolytic Capacitor [capacitance=0.1mF voltage=35V package="100 mil [THT, electrolytic]"]
  120k = Resistor [tolerance=±1% power=0.25W resistance=100k package=THT]
  bat46 = Diode [package=diode-1n4148]
  bat46_2 = Diode [package=diode-1n4148]
  bat46_3 = Diode [package=diode-1n4148]
  bat46_4 = Diode [package=diode-1n4148]
  100K1 = Resistor [tolerance=±5% resistance=100k power=0.25W package=THT]  # not connected
  4_7k = Resistor [tolerance=±5% power=0.25W resistance=4.7k package=THT]  # not connected
  1nF = Ceramic Capacitor [capacitance=1nF voltage=16V package="200 mil [THT, multilayer]"]
  1nF1 = Ceramic Capacitor [capacitance=1nF voltage=16V package="200 mil [THT, multilayer]"]
  1nF2 = Ceramic Capacitor [capacitance=1nF voltage=16V package="200 mil [THT, multilayer]"]
  S1 = SWITCH-DPDT-latching [package=os]
  S2 = SWITCH-DPDT-latching [package=os]
  S3 = SWITCH-DPDT-latching [package=os]  # not connected
  S4 = SWITCH-DPDT-latching [package=os]  # not connected
  1nF3 = Ceramic Capacitor [capacitance=1nF voltage=16V package="200 mil [THT, multilayer]"]
  2_2n = Ceramic Capacitor [capacitance=2.2nF voltage=16V package="200 mil [THT, multilayer]"]
  2_2n_2 = Ceramic Capacitor [capacitance=2.2nF voltage=16V package="200 mil [THT, multilayer]"]
  2_2n_3 = Ceramic Capacitor [capacitance=2.2nF voltage=16V package="200 mil [THT, multilayer]"]
  120k_2 = Resistor [tolerance=±1% power=0.25W resistance=100k package=THT]
  120k_3 = Resistor [tolerance=±1% power=0.25W resistance=100k package=THT]
  120k_4 = Resistor [tolerance=±1% power=0.25W resistance=100k package=THT]
  1M = Resistor [tolerance=±1% power=0.25W resistance=1M package=THT]
  103_2 = Ceramic Capacitor [capacitance=10nF voltage=16V package="200 mil [THT, multilayer]"]
  1M_2 = Resistor [tolerance=±1% power=0.25W resistance=1M package=THT]
  1M_3 = Resistor [tolerance=±1% power=0.25W resistance=1M package=THT]
  1M_4 = Resistor [tolerance=±1% power=0.25W resistance=1M package=THT]
  4_7n = Ceramic Capacitor [capacitance=4.7nF voltage=16V package="200 mil [THT, multilayer]"]
  4_7n_2 = Ceramic Capacitor [capacitance=4.7nF voltage=16V package="200 mil [THT, multilayer]"]
  10nF = Ceramic Capacitor [capacitance=10nF voltage=16V package="200 mil [THT, multilayer]"]
  120k_5 = Resistor [tolerance=±1% power=0.25W resistance=100k package=THT]
  120k_6 = Resistor [tolerance=±1% power=0.25W resistance=100k package=THT]
  10K = Resistor [tolerance=±1% power=0.25W resistance=10k package=THT]
  LM3900 = LM3900 [chip_label=LM3900 package="DIP (Dual Inline) [THT]"]
  4_7n_3 = Ceramic Capacitor [capacitance=4.7nF voltage=16V package="200 mil [THT, multilayer]"]
  4_7n_4 = Ceramic Capacitor [capacitance=4.7nF voltage=16V package="200 mil [THT, multilayer]"]
  120k3 = Resistor [tolerance=±1% power=0.25W resistance=100k package=THT]
  10K1 = Resistor [tolerance=±1% power=0.25W resistance=10k package=THT]
  120k4 = Resistor [tolerance=±1% power=0.25W resistance=100k package=THT]

nets:
  GND: ][1.Pin_1, 103.0, 104.1, J3.pin2, J3.pin3, J3.pin4, J3.pin13, J3.pin14, J3.pin15, Out1.Pin_1, OUT2.Pin_1, OUT2.Pin_3, ][2.Pin_1, Out3.Pin_1, IN3.Pin_1, IN4.Pin_1, TL074.connector10, OUT4.Pin_1, 100uF.-, 103_2.1, 10K.Pin_0, LM3900.GND, 10K1.Pin_1
  N1: ][1.Pin_3, 1nF.0
  N2: 103.1, 104.0, 4001.C, TL074.connector3, 100uF.+, 1M.Pin_0, 103_2.0, 1M_2.Pin_0, 1M_3.Pin_0, 1M_4.Pin_0, LM3900.Vcc
  N3: J3.pin1, J3.pin16
  9V: J3.pin5, J3.pin6, J3.pin11, J3.pin12, 4001.A
  N4: J3.pin7, J3.pin10
  N5: J3.pin8, J3.pin9
  N6: ][2.Pin_3, 1nF3.0
  N7: IN3.Pin_3, 1nF1.0
  N8: IN4.Pin_3, 1nF2.0
  N9: 120k.Pin_1, bat46.C
  N10: bat46.A, 1nF2.1
  N11: bat46_2.A, 1nF3.1
  N12: bat46_2.C, 120k_4.Pin_1
  N13: bat46_3.A, 1nF1.1
  N14: bat46_3.C, 120k_2.Pin_0
  N15: bat46_4.A, 1nF.1
  N16: bat46_4.C, 120k_3.Pin_0
  N17: S1.1, 2_2n.0
  N18: S1.2, 2_2n_2.0, 2_2n_3.0, 10K.Pin_1
  N19: S1.3, 4_7n.1
  N20: S1.4, 4_7n.0
  N21: S1.5, 120k_5.Pin_0, 120k_6.Pin_0
  N22: S1.6, 2_2n.1
  N23: S2.1, 4_7n_2.0
  N24: S2.2, 4_7n_3.1, 4_7n_4.1, 10K1.Pin_0
  N25: S2.3, 10nF.1
  N26: S2.4, 10nF.0
  N27: S2.5, 120k3.Pin_1, 120k4.Pin_1
  N28: S2.6, 4_7n_2.1
  N29: 2_2n_2.1, 120k_6.Pin_1, LM3900.1IN-
  N30: 2_2n_3.1, 120k_5.Pin_1, LM3900.1OUT
  N31: 1M.Pin_1, LM3900.1IN+
  N32: 1M_2.Pin_1, LM3900.2IN+
  N33: 1M_3.Pin_1, LM3900.3IN+
  N34: 1M_4.Pin_1, LM3900.4IN+
  N35: LM3900.2IN-, 4_7n_3.0, 120k4.Pin_0
  N36: LM3900.2OUT, 4_7n_4.0, 120k3.Pin_0

notes:
  frame
  blueprint@poetaster . de 2025
  jlcjlcjlcjlcjlc

custom parts:
  PJ-301M: Phone power jack.
  TL074 Quad Opamp (Movable): Quadruple Operational Amplifier (Opamp)
  TL074 Quad Opamp (Movable): Quadruple Operational Amplifier (Opamp)
  TL074 Quad Opamp (Movable): Quadruple Operational Amplifier (Opamp)
  TL074 Quad Opamp (Movable): Quadruple Operational Amplifier (Opamp)
  TL074 Quad Opamp (Movable): Quadruple Operational Amplifier (Opamp)
  TL074 Quad Opamp (Movable): Quadruple Operational Amplifier (Opamp)
  SWITCH-DPDT-latching: DPDT latching pushbutton switch
  LM3900: A DIP stand-in part for whatever IC you want. With 14 pins on a 300mil dual inline package (DIP) footprint.
